// Logisim project Water Level Monitoring System.circ as structural Verilog: 1 circuit, main circuit main
module main (
  input  in_1,
  output Green_Light,
  output Yellow_Light,
  output out_4,
  output Buzzer
);

  wire and_1_out, and_2_out, and_3_out, and_4_out, button_1_out, clock_1_out, d_ff_1_qn,
       demultiplexer_1_out0, demultiplexer_1_out1, demultiplexer_1_out2, nor_1_out, or_1_out, or_2_out,
       xnor_1_out, xor_1_out;
  wire [1:0] d_ff_1_q;

  D_Flip_Flop d_ff_1 (
    .clk(clock_1_out), .D(d_ff_1_qn), .Q(d_ff_1_q[0]), .Qn(d_ff_1_qn), .reset(button_1_out));  // open: preset, en
  xor xor_1 (xor_1_out, d_ff_1_q[0], d_ff_1_q[1]);
  D_Flip_Flop d_ff_2 (.clk(clock_1_out), .D(xor_1_out), .Q(d_ff_1_q[1]), .reset(button_1_out));  // open: Qn, preset, en
  Demultiplexer #(.select(2), .enable("false")) demultiplexer_1 (
    .out0(demultiplexer_1_out0), .out1(demultiplexer_1_out1), .out2(demultiplexer_1_out2), .in(in_1),
    .sel(d_ff_1_q));  // open: out3
  or or_1 (or_1_out, demultiplexer_1_out0, demultiplexer_1_out1, demultiplexer_1_out2);
  or or_2 (or_2_out, demultiplexer_1_out1, demultiplexer_1_out2);
  xnor xnor_1 (xnor_1_out, 1'b1, nor_1_out);
  and and_1 (and_1_out, xnor_1_out, or_1_out);
  and and_2 (and_2_out, and_1_out, or_2_out);
  and and_3 (and_3_out, and_2_out, demultiplexer_1_out2);
  and and_4 (and_4_out, and_3_out, and_2_out, and_1_out);
  Clock clock_1 (.out(clock_1_out));
  Button button_1 (.out(button_1_out));
  D_Flip_Flop d_ff_3 (
    .clk(clock_1_out), .D(and_1_out), .Q(Green_Light), .preset(button_1_out), .en(1'b1), .reset(button_1_out));  // open: Qn
  D_Flip_Flop d_ff_4 (
    .clk(clock_1_out), .D(and_2_out), .Q(Yellow_Light), .preset(button_1_out), .en(1'b1), .reset(button_1_out));  // open: Qn
  D_Flip_Flop d_ff_5 (
    .clk(clock_1_out), .D(and_3_out), .Q(out_4), .preset(button_1_out), .en(1'b1), .reset(button_1_out));  // open: Qn
  D_Flip_Flop d_ff_6 (
    .clk(clock_1_out), .D(and_4_out), .Q(Buzzer), .preset(button_1_out), .en(1'b1), .reset(button_1_out));  // open: Qn
  LED led_1 (.in(Green_Light));
  LED led_2 (.in(Yellow_Light));
  LED led_3 (.in(out_4));
  LED led_4 (.in(Buzzer));
  nor nor_1 (nor_1_out, out_4, Buzzer);

  // Notes on the sheet:
  //   Counter For Selection Line
  //   Demux For Automatic Input
  //   Power
  //   Clock
  //   Second Inout From the Last NOR to shut down the whle circuit When all Outputs are 1
  //   Reset
  //   Enabler
  //   Red Light
  //   NOR 
endmodule
